# Fritzing sketch Shield_attiny (saved by Fritzing 0.9.0b)
circuit board: 10cm x 7cm

parts:
  Componente1 = Arduino Uno (Rev3)
  Pololu_A1 = Pololu A4988 [package=SO16]
  Pololu_A2 = Pololu A4988 [package=SO16]
  J2 = screw terminal, 4 pins
  J1 = screw terminal, 4 pins
  Power_plug1 = Power plug
  U1 = ATTINY45 [package=dip]
  J6 = female pin header, 3 pins [form="♀ (female)"]
  J7 = female pin header, 3 pins [form="♀ (female)"]
  J8 = female pin header, 3 pins [form="♀ (female)"]
  LED1 = LED - 5mm [color="Red (633nm)" package="5 mm [THT]"]
  R1 = Resistor [tolerance=±5% resistance=220 package=THT]
  LED2 = LED - 5mm [color="Red (633nm)" package="5 mm [THT]"]
  R2 = Resistor [tolerance=±5% resistance=220 package=THT]
  J9 = female pin header, 2 pins [form="♀ (female)"]
  C1 = Electrolytic Capacitor [capacitance=1µF package="100 mil [THT, electrolytic]"]
  J10 = female pin header, 2 pins [form="♀ (female)"]

nets:
  N1: Componente1.D8, Pololu_A1.ENABLE, Pololu_A2.ENABLE
  N2: Componente1.D13/SCK, U1.PB4(ADC2)
  GND: Componente1.GND, Pololu_A1.GND, Pololu_A2.GND, Power_plug1.GND, U1.GND, J6.pin1, R1.Pin_1, R2.Pin_1, J9.pin2, C1.-, J10.pin2
  N3: Componente1.D2, Pololu_A2.STEP
  N4: Componente1.D3_PWM, Pololu_A1.STEP
  N5: Componente1.D5_PWM, Pololu_A2.DIR
  N6: Componente1.D6_PWM, Pololu_A1.DIR
  VDD: Componente1.5V, Pololu_A1.VDD, Pololu_A2.MS1, Pololu_A2.VDD, U1.VCC, J6.pin2, J8.pin3, LED2.anode, J9.pin1
  N7: Pololu_A1.MS1, J7.pin1
  N8: Pololu_A1.MS2, J7.pin2
  N9: Pololu_A1.MS3, J7.pin3
  N10: Pololu_A1.RESET, Pololu_A1.SLEEP
  N11: Pololu_A1.1B, J1.pin4
  N12: Pololu_A1.1A, J1.pin3
  N13: Pololu_A1.2A, J1.pin2
  N14: Pololu_A1.2B, J1.pin1
  N15: Pololu_A1.VMOT, Pololu_A2.VMOT, Power_plug1.VCC, LED1.anode, C1.+, J10.pin1
  N16: Pololu_A2.MS2, J8.pin2
  N17: Pololu_A2.MS3, J8.pin1
  N18: Pololu_A2.RESET, Pololu_A2.SLEEP
  N19: Pololu_A2.1B, J2.pin4
  N20: Pololu_A2.1A, J2.pin3
  N21: Pololu_A2.2A, J2.pin2
  N22: Pololu_A2.2B, J2.pin1
  N23: U1.PB3(ADC3), J6.pin3
  N24: LED1.cathode, R1.Pin_0
  N25: LED2.cathode, R2.Pin_0
